// Digital circuit hdl_test.dig as structural Verilog
module hdl_test (
  input  Clock,
  input  BTN0,
  input  BTN1,
  output LED0,
  output LED1,
  output LED2,
  output LED3
);

  Counter #(.Bits(4)) counter_1 (.en(BTN0), .C(Clock), .clr(BTN1), .out({LED3, LED2, LED1, LED0}));  // open: ovf

  // Notes on the sheet:
  //   LED0: pin H5
  //   LED1: pin J5
  //   LED2: pin T9
  //   LED3: pin T10
  //   Clock: pin W3, Hz: 10
  //   BTN0: pin D9
  //   BTN1: pin C9
  //   LED's
endmodule
